# Fritzing sketch Gamecube (saved by Fritzing 0.9.1b)
breadboards: 1

parts:
  Bauteil1 = Arduino Uno (Rev3)
  Bauteil2 = Logic Level Converter
  S1 = Pushbutton [package="[THT]"]
  R1 = Resistor [tolerance=±5% resistance=1k package=THT]

nets:
  N1: Bauteil1.D8, S1.Pin_3, S1.Pin_4
  N2: Bauteil1.D4, Bauteil2.TX2_HV
  N3: Bauteil1.3V3, Bauteil2.LV, R1.Pin_1
  N4: Bauteil1.5V, Bauteil2.HV
  GND: Bauteil1.GND, Bauteil2.GND, S1.Pin_1, S1.Pin_2
  N5: Bauteil2.TX2_LV, R1.Pin_0

notes:
  Cables connected with the Gamecube Controller.
  Pay attention to different cable colors.
